// Logisim project ALU.circ as structural Verilog: 1 circuit, main circuit main
module main (
  input  in_1,
  input  in_2,
  input  [1:0] Op,
  output out_4,
  output out_5
);

  wire adder_1_out, and_1_out, or_1_out, xor_1_out;

  and and_1 (and_1_out, in_1, in_2);
  or or_1 (or_1_out, in_1, in_2);
  Adder #(.width(1)) adder_1 (.a(in_1), .b(in_2), .out(adder_1_out), .cin(1'b0), .cout(out_5));
  xor xor_1 (xor_1_out, in_1, in_2);
  Multiplexer #(.enable("false"), .select(2)) multiplexer_1 (
    .in0(and_1_out), .in1(or_1_out), .in2(adder_1_out), .in3(xor_1_out), .out(out_4), .sel(Op));

  // Notes on the sheet:
  //   AND op code 00
  //   OR op code 01
  //   SUM op code 10
  //   XOR op code 11
  //   ALU
  //   Assembly
  //   Data Line => 10
  //   AND a b
  //   Assembler
  //   Instruction => 00
  //   Instruction => Compiler => sequence of 0's and 1's
  //   0010 0011 1011 0101 1010 
endmodule
