// Logisim project intro.circ as structural Verilog: 1 circuit, main circuit main
module main (
  input  AND_A,
  input  AND_B,
  input  OR_A,
  input  OR_B,
  input  NOT_A,
  input  A,
  input  B,
  input  C,
  output AND_Q,
  output OR_Q,
  output NOT_Q,
  output F
);

  wire and_2_out;

  and and_1 (AND_Q, AND_A, AND_B);
  or or_1 (OR_Q, OR_A, OR_B);
  not not_1 (NOT_Q, NOT_A);
  and and_2 (and_2_out, A, B);
  and and_3 (F, and_2_out, C);

  // Notes on the sheet:
  //   AND
  //   OR
  //   NOT
endmodule
