// Logisim project intro2.circ as structural Verilog: 1 circuit, main circuit main
module main (
  input  A,
  input  B,
  input  C,
  input  in_4,
  input  in_5,
  input  in_6,
  input  in_7,
  input  in_8,
  input  in_9,
  input  Input_A,
  input  AND_Input_A,
  output E,
  output out_13,
  output out_14,
  output out_15,
  output out_16,
  output out_17
);

  wire and_1_out, and_2_out, and_3_out, and_4_out, and_6_out, and_7_out, and_8_out, not_1_out, not_2_out,
       not_3_out, not_4_out, not_5_out, or_2_out;

  not not_1 (not_1_out, A);
  not not_2 (not_2_out, B);
  not not_3 (not_3_out, C);
  and and_1 (and_1_out, in_4, in_5);
  nand nand_1 (out_14, in_6, in_7);
  nor nor_1 (out_15, in_8, in_9);
  not not_4 (not_4_out, Input_A);
  not not_5 (not_5_out, AND_Input_A);
  and and_2 (and_2_out, not_1_out, B);
  and and_3 (and_3_out, A, not_2_out);
  and and_4 (and_4_out, A, B);
  not not_6 (out_13, and_1_out);
  or or_1 (out_16, not_4_out, Input_A);
  and and_5 (out_17, not_5_out, AND_Input_A);
  and and_6 (and_6_out, and_2_out, C);
  or or_2 (or_2_out, and_6_out, and_7_out);
  and and_7 (and_7_out, and_3_out, C);
  and and_8 (and_8_out, and_4_out, not_3_out);
  or or_3 (E, or_2_out, and_8_out);
endmodule
