// Logisim project kmap.circ as structural Verilog: 1 circuit, main circuit main
module main (
  input  A,
  input  B,
  input  in_3,
  input  in_4,
  output out_5,
  output out_6
);

  wire and_1_out, not_1_out, not_2_out, or_1_out;

  not not_1 (not_1_out, A);
  or or_1 (or_1_out, A, B);
  or or_2 (out_6, in_3, in_4);
  not not_2 (not_2_out, or_1_out);
  and and_1 (and_1_out, not_1_out, not_2_out);
  not not_3 (out_5, and_1_out);
endmodule
