// Logisim project kmap2.circ as structural Verilog: 1 circuit, main circuit main
module main (
  input  A,
  input  B,
  input  C,
  input  x_A,
  input  x_B,
  input  x_C,
  input  z_A,
  input  z_B,
  input  z_C,
  input  a_A,
  input  a_B,
  input  a_C,
  input  v_A,
  input  v_B,
  input  v_C,
  output out_16,
  output out_17,
  output out_18,
  output out_19,
  output out_20
);

  wire and_1_out, and_2_out, and_3_out, and_5_out, and_6_out, not_1_out, not_2_out, not_3_out, not_4_out,
       not_5_out, not_6_out, or_3_out, or_6_out;

  not not_1 (not_1_out, v_A);
  not not_2 (not_2_out, v_C);
  not not_3 (not_3_out, A);
  not not_4 (not_4_out, C);
  not not_5 (not_5_out, z_C);
  not not_6 (not_6_out, a_B);
  and and_1 (and_1_out, not_3_out, B);
  and and_2 (and_2_out, not_3_out, B);
  or or_1 (out_17, x_A, x_B);
  or or_2 (out_18, z_A, not_5_out);
  or or_3 (or_3_out, not_6_out, a_C);
  and and_3 (and_3_out, not_1_out, v_B);
  and and_4 (out_16, and_1_out, not_4_out);
  and and_5 (and_5_out, and_2_out, C);
  and and_6 (and_6_out, v_B, not_2_out);
  or or_4 (out_19, a_A, or_3_out);
  or or_5 (out_20, and_3_out, and_6_out);
  or or_6 (or_6_out, out_16, and_5_out);
  // also tied to GND on the sheet: {x_C, z_B}
endmodule
