// Logisim project memory_elements.circ as structural Verilog: 1 circuit, main circuit main
module main (
  input  R,
  input  S,
  input  C,
  input  D,
  output Q,
  output NO_Q,
  output out_7,
  output out_8
);

  wire and_1_out, and_2_out, not_1_out;

  not not_1 (not_1_out, D);
  and and_1 (and_1_out, C, not_1_out);
  and and_2 (and_2_out, C, D);
  nor nor_1 (Q, R, NO_Q);
  nor nor_2 (NO_Q, Q, S);
  nor nor_3 (out_7, and_1_out, out_8);
  nor nor_4 (out_8, out_7, and_2_out);
endmodule
