// Logisim project simple_adder.circ as structural Verilog: 1 circuit, main circuit main
module main (
  input  a0,
  input  a1,
  input  b0,
  input  b1,
  input  in_5,
  input  in_6,
  input  in_7,
  input  in_8,
  input  in_9,
  input  [1:0] in_10,
  input  [1:0] in_11,
  input  [1:0] in_12,
  input  [1:0] in_13,
  input  [1:0] in_14,
  input  [1:0] in_15,
  input  [1:0] in_16,
  input  [1:0] input_0,
  input  [1:0] input_1,
  input  selector,
  output Sum_1,
  output Sum_0,
  output Cout_1,
  output out_23,
  output x_SUM,
  output x_COUT,
  output out_26,
  output [1:0] out_27,
  output [1:0] out_28,
  output [1:0] out_29,
  output out_30,
  output out_31,
  output out_32,
  output out_33,
  output out_34,
  output [1:0] out_35
);

  wire adder_5_cout, and_1_out, and_2_out, and_3_out, and_5_out, and_6_out, and_7_out, or_2_out, xor_1_out,
       xor_2_out, xor_6_out;

  xor xor_1 (xor_1_out, a1, b1);
  and and_1 (and_1_out, or_2_out, a1);
  and and_2 (and_2_out, or_2_out, b1);
  and and_3 (and_3_out, a1, b1);
  xor xor_2 (xor_2_out, in_5, in_6);
  Decoder #(.select(2)) decoder_1 (
    .out0(out_31), .out1(out_32), .out2(out_33), .out3(out_34), .sel(in_16));  // open: en
  Multiplexer #(.enable("false")) multiplexer_1 ();  // open: in0, in1, out, sel
  xor xor_3 (Sum_1, xor_1_out, or_2_out);
  or or_1 (Cout_1, and_1_out, and_2_out, and_3_out);
  xor xor_4 (x_SUM, in_8, in_9);
  and and_4 (x_COUT, in_8, in_9);
  Multiplexer #(.enable("false"), .width(2)) multiplexer_2 (.in0(input_0), .in1(input_1), .out(out_35), .sel(selector));
  xor xor_5 (out_23, xor_2_out, in_7);
  Adder #(.width(2)) adder_1 (.a(in_12), .b(in_14), .out(out_28), .cin(adder_5_cout), .cout(out_30));
  Adder adder_2 ();  // open: a, b, out, cin, cout
  Adder adder_3 ();  // open: a, b, out, cin, cout
  Adder #(.width(2)) adder_4 (.a(in_10), .b(in_11), .out(out_27), .cin(1'b0), .cout(out_26));
  Adder #(.width(2)) adder_5 (.a(in_13), .b(in_15), .out(out_29), .cin(1'b0), .cout(adder_5_cout));
  Adder adder_6 ();  // open: a, b, out, cin, cout
  xor xor_6 (xor_6_out, a0, b0);
  and and_5 (and_5_out, 1'b0, a0);
  and and_6 (and_6_out, 1'b0, b0);
  and and_7 (and_7_out, a0, b0);
  Adder adder_7 ();  // open: a, b, out, cin, cout
  xor xor_7 (Sum_0, xor_6_out, 1'b0);
  or or_2 (or_2_out, and_5_out, and_6_out, and_7_out);

  // Notes on the sheet:
  //   1-bit adder
  //   HALF ADDER
  //   11
  //   01
  //   00
endmodule
