// Logisim project traffic_light.circ as structural Verilog: 1 circuit, main circuit main
module main (
  input  a,
  input  b,
  output G,
  output Y,
  output R
);

  wire and_2_out, and_3_out, not_1_out, not_2_out;

  not not_1 (not_1_out, a);
  not not_2 (not_2_out, b);
  and and_1 (G, a, b);
  and and_2 (and_2_out, not_1_out, b);
  and and_3 (and_3_out, a, not_2_out);
  and and_4 (R, not_1_out, not_2_out);
  or or_1 (Y, and_2_out, and_3_out);
endmodule
